// Logisim project MIPS-like.circ as structural Verilog: 5 circuits, main circuit main
module main (
  output [2:0] out_1,
  output [2:0] out_2,
  output [1:0] out_3
);

  wire ALUSrc, and_1_out, Branch, clear, clock, Jump, MemRead, MemToReg, MemWrite, not_1_out, or_1_out,
       RegDst, RegWrite, tunnel;
  wire [3:0] multiplexer_2_out;
  wire [4:0] rom_1_data;
  wire [7:0] bit_extender_1_out;
  wire [23:0] adder_1_out, Address, bit_extender_3_out, multiplexer_4_out, PC, PCAddress;
  wire [31:0] bit_extender_2_out, multiplexer_3_out, R1, R2, ram_1_data, ULAOut, WriteData;

  Clock clock_1 (.out(clock));
  Button button_1 (.out(clear));
  Unidade_de_Controle unidade_de_controle_1 (
    .bit0(out_2[2]), .bit1(out_2[1]), .bit2(out_2[0]), .RegDst(RegDst), .RegWrite(RegWrite), .ALUSrc(ALUSrc),
    .MemWrite(MemWrite), .MemRead(MemRead), .MemToReg(MemToReg), .Branch(Branch), .Jump(Jump),
    .ALUOp0(out_3[1]), .ALUOp1(out_3[0]));
  Bit_Extender #(.in_width(32), .out_width(8), .\type ("zero")) bit_extender_1 (.in(ULAOut), .out(bit_extender_1_out));
  not not_1 (not_1_out, clock);
  RAM #(.dataWidth(32), .bus("separate"), .simpleMode("false"), .Select("low")) ram_1 (
    .addr(bit_extender_1_out), .din(R2), .data(ram_1_data), .str(MemWrite), .clk(not_1_out), .clr(clear));  // open: sel, ld
  ROM #(.addrWidth(24), .dataWidth(32), .Select("high")) rom_1 (.addr(PC), .data({out_2, Address, rom_1_data}));
  Multiplexer #(.width(32), .enable("false")) multiplexer_1 (
    .in0(ram_1_data), .in1(ULAOut), .out(WriteData), .sel(MemToReg));
  Controle_ULA controle_ula_1 (.Func(Address[6:4]), .ALUop(out_3), .ALUCtrl(out_1));
  Multiplexer #(.width(4), .enable("false")) multiplexer_2 (
    .in0(Address[19:16]), .in1(Address[15:12]), .out(multiplexer_2_out), .sel(RegDst));
  assign bit_extender_2_out = {{16{1'b0}}, Address[15:0]};  // Bit_Extender bit_extender_2
  Adder #(.width(24)) adder_1 (.a(24'h1), .b(PC), .out(adder_1_out));  // open: cin, cout
  Multiplexer #(.width(32), .enable("false")) multiplexer_3 (
    .in0(R2), .in1(bit_extender_2_out), .out(multiplexer_3_out), .sel(ALUSrc));
  ULA ula_1 (
    .Data_0(R1), .Data_1(multiplexer_3_out), .Shamt(Address[11:7]), .Func(out_1), .out_5(tunnel),
    .Resultado(ULAOut));
  Register #(.width(24), .Select("low")) register_1 (.D(PCAddress), .Q(PC), .clk(clock), .clr(clear));  // open: en
  assign bit_extender_3_out = {{8{1'b0}}, Address[15:0]};  // Bit_Extender bit_extender_3
  Banco_de_Registradores banco_de_registradores_1 (
    .Read_register_1(Address[23:20]), .Read_register_2(Address[19:16]), .Write_register(multiplexer_2_out),
    .Write_data(WriteData), .CLOCK(clock), .CLEAR(clear), .RW(RegWrite), .Read_data_1(R1), .Read_data_2(R2));
  Multiplexer #(.width(24), .enable("false")) multiplexer_4 (
    .in0(Address), .in1(bit_extender_3_out), .out(multiplexer_4_out), .sel(Branch));
  or or_1 (or_1_out, Jump, and_1_out);
  Multiplexer #(.width(24), .enable("false")) multiplexer_5 (
    .in0(adder_1_out), .in1(multiplexer_4_out), .out(PCAddress), .sel(or_1_out));
  and and_1 (and_1_out, tunnel, Branch);

  // Other names for the same wires on the sheet: Imm[15:0] = Address[15:0]; Func[2:0] = Address[6:4];
  //   Shamt[4:0] = Address[11:7]; RD[3:0] = Address[15:12]; RT[3:0] = Address[19:16]; RS[3:0] = Address[23:20];
  //   OPCode[2:0] = out_2; ALUOp[1:0] = out_3; ULA_C[2:0] = out_1

  // Notes on the sheet:
  //   CLOCK E CLEAR
  //   CONTROL UNIT
  //   DATA MEMORY
  //   INSTRUCTION MEMORY
  //   contents of rom_1 (hex, n*v repeats v):
  //   20000080 22200000 24400200 26600400 5e800600 880003e0 5ea00600 8a0003a0 5ec00600 5ee00600 8e0002e0
  //   8100200 10f00000 10300000 51200000 e140200 14b40000 14540000 55600000 13720200 12cc0000 2ee00020
  //   a0000140 8180200 18b80000 18780000 78c00000 2aa00020 a00000e0 28800020 a00000a0 3dc00020 7fc00620
  //   ULA CONTROL
  //   BANCO DE REGISTRADORES
  //   ULA
  //   PROGRAM COUNTER
endmodule

module Banco_de_Registradores (
  input  [3:0] Read_register_1,
  input  [3:0] Read_register_2,
  input  [3:0] Write_register,
  input  [31:0] Write_data,
  input  CLOCK,
  input  CLEAR,
  input  RW,
  output [31:0] Read_data_1,
  output [31:0] Read_data_2
);

  wire WE0, WE1, WE2, WE3, WE4, WE5, WE6, WE7, WE8, WE9, WE10, WE11, WE12, WE13, WE14, WE15;
  wire [31:0] Reg0, Reg1, Reg2, Reg3, Reg4, Reg5, Reg6, Reg7, Reg8, Reg9, Reg10, Reg11, Reg12, Reg13, Reg14,
       Reg15;

  Demultiplexer #(.select(4), .enable("false")) demultiplexer_1 (
    .out0(WE0), .out1(WE1), .out2(WE2), .out3(WE3), .out4(WE4), .out5(WE5), .out6(WE6), .out7(WE7),
    .out8(WE8), .out9(WE9), .out10(WE10), .out11(WE11), .out12(WE12), .out13(WE13), .out14(WE14),
    .out15(WE15), .in(RW), .sel(Write_register));
  Multiplexer #(.select(4), .width(32), .enable("false")) multiplexer_1 (
    .in0(Reg0), .in1(Reg1), .in2(Reg2), .in3(Reg3), .in4(Reg4), .in5(Reg5), .in6(Reg6), .in7(Reg7),
    .in8(Reg8), .in9(Reg9), .in10(Reg10), .in11(Reg11), .in12(Reg12), .in13(Reg13), .in14(Reg14),
    .in15(Reg15), .out(Read_data_1), .sel(Read_register_1));
  Register #(.width(32), .Select("low")) register_1 (.D(Write_data), .en(WE0), .Q(Reg0), .clk(CLOCK), .clr(CLEAR));
  Register #(.width(32), .Select("low")) register_2 (.D(Write_data), .en(WE1), .Q(Reg1), .clk(CLOCK), .clr(CLEAR));
  Register #(.width(32), .Select("low")) register_3 (.D(Write_data), .en(WE2), .Q(Reg2), .clk(CLOCK), .clr(CLEAR));
  Register #(.width(32), .Select("low")) register_4 (.D(Write_data), .en(WE3), .Q(Reg3), .clk(CLOCK), .clr(CLEAR));
  Register #(.width(32), .Select("low")) register_5 (.D(Write_data), .en(WE4), .Q(Reg4), .clk(CLOCK), .clr(CLEAR));
  Register #(.width(32), .Select("low")) register_6 (.D(Write_data), .en(WE5), .Q(Reg5), .clk(CLOCK), .clr(CLEAR));
  Register #(.width(32), .Select("low")) register_7 (.D(Write_data), .en(WE6), .Q(Reg6), .clk(CLOCK), .clr(CLEAR));
  Register #(.width(32), .Select("low")) register_8 (.D(Write_data), .en(WE7), .Q(Reg7), .clk(CLOCK), .clr(CLEAR));
  Register #(.width(32), .Select("low")) register_9 (.D(Write_data), .en(WE8), .Q(Reg8), .clk(CLOCK), .clr(CLEAR));
  Register #(.width(32), .Select("low")) register_10 (.D(Write_data), .en(WE9), .Q(Reg9), .clk(CLOCK), .clr(CLEAR));
  Register #(.width(32), .Select("low")) register_11 (.D(Write_data), .en(WE10), .Q(Reg10), .clk(CLOCK), .clr(CLEAR));
  Register #(.width(32), .Select("low")) register_12 (.D(Write_data), .en(WE11), .Q(Reg11), .clk(CLOCK), .clr(CLEAR));
  Register #(.width(32), .Select("low")) register_13 (.D(Write_data), .en(WE12), .Q(Reg12), .clk(CLOCK), .clr(CLEAR));
  Register #(.width(32), .Select("low")) register_14 (.D(Write_data), .en(WE13), .Q(Reg13), .clk(CLOCK), .clr(CLEAR));
  Register #(.width(32), .Select("low")) register_15 (.D(Write_data), .en(WE14), .Q(Reg14), .clk(CLOCK), .clr(CLEAR));
  Register #(.width(32), .Select("low")) register_16 (.D(Write_data), .en(WE15), .Q(Reg15), .clk(CLOCK), .clr(CLEAR));
  Multiplexer #(.select(4), .width(32), .enable("false")) multiplexer_2 (
    .in0(Reg0), .in1(Reg1), .in2(Reg2), .in3(Reg3), .in4(Reg4), .in5(Reg5), .in6(Reg6), .in7(Reg7),
    .in8(Reg8), .in9(Reg9), .in10(Reg10), .in11(Reg11), .in12(Reg12), .in13(Reg13), .in14(Reg14),
    .in15(Reg15), .out(Read_data_2), .sel(Read_register_2));

  // Other names for the same wires on the sheet: CLK = CLOCK; Data[31:0] = Write_data; Read_1[3:0] = Read_register_1;
  //   Read_2[3:0] = Read_register_2; WR[3:0] = Write_register

  // Notes on the sheet:
  //   ENTRADAS
  //   SELEÇÃO DE REGISTRADOR
  //   SAÍDA REGISTRADOR 1
  //   REGISTRADORES
  //   SAÍDA REGISTRADOR 2
endmodule

module ULA (
  input  [31:0] Data_0,
  input  [31:0] Data_1,
  input  [4:0] Shamt,
  input  [2:0] Func,
  output out_5,
  output [31:0] Resultado
);

  wire Igualdade, tunnel;
  wire [31:0] AComp, AMult, AShiftEsq, ASoma, BComp, BMult, BSoma, CompSaida, MultSaida, ShiftEsqSaida,
       SomaSaida;

  Demultiplexer #(.select(3), .width(32), .enable("false")) demultiplexer_1 (
    .out0(ASoma), .out1(AMult), .out2(AShiftEsq), .out3(AComp), .in(Data_0), .sel(Func));  // open: out4, out5, out6, out7
  Demultiplexer #(.select(3), .width(32), .enable("false")) demultiplexer_2 (
    .out0(BSoma), .out1(BMult), .out3(BComp), .in(Data_1), .sel(Func));  // open: out2, out4, out5, out6, out7
  Adder #(.width(32)) adder_1 (.a(ASoma), .b(BSoma), .out(SomaSaida));  // open: cin, cout
  Multiplier #(.width(32)) multiplier_1 (.a(AMult), .b(BMult), .out(MultSaida));  // open: cin, cout
  Shifter #(.width(32)) shifter_1 (.in(AShiftEsq), .\dist (Shamt), .out(ShiftEsqSaida));
  Comparator #(.width(32)) comparator_1 (.a(AComp), .b(BComp), .gt(tunnel), .eq(Igualdade));  // open: lt
  assign CompSaida = {{31{1'b0}}, Igualdade};  // Bit_Extender bit_extender_1
  or or_1 (out_5, tunnel, Igualdade);
  Multiplexer #(.select(3), .width(32), .enable("false")) multiplexer_1 (
    .in0(SomaSaida), .in1(MultSaida), .in2(ShiftEsqSaida), .in3(CompSaida), .out(Resultado), .sel(Func));  // open: in4, in5, in6, in7

  // Other names for the same wires on the sheet: A[31:0] = Data_0; B[31:0] = Data_1

  // Notes on the sheet:
  //   ENTRADAS
endmodule

module Controle_ULA (
  input  [2:0] Func,
  input  [1:0] ALUop,
  output [2:0] ALUCtrl
);

  Multiplexer #(.select(2), .width(3), .enable("false")) multiplexer_1 (
    .in0(3'b000), .in1(3'b011), .in2(Func), .in3(3'b000), .out(ALUCtrl), .sel(ALUop));

  // Notes on the sheet:
  //   LW/SW
  //   BGE
  //   ADDI
endmodule

module Unidade_de_Controle (
  input  bit0,
  input  bit1,
  input  bit2,
  output RegDst,
  output RegWrite,
  output ALUSrc,
  output MemWrite,
  output MemRead,
  output MemToReg,
  output Branch,
  output Jump,
  output ALUOp0,
  output ALUOp1
);

  wire and_3_out, and_4_out, and_5_out, and_6_out, and_10_out, not_1_out, not_2_out, not_3_out, not_4_out,
       not_5_out, not_6_out, not_7_out, not_9_out, not_10_out, not_11_out, not_12_out;

  not not_1 (not_1_out, bit0);
  not not_2 (not_2_out, bit1);
  not not_3 (not_3_out, bit2);
  not not_4 (not_4_out, bit0);
  not not_5 (not_5_out, bit1);
  not not_6 (not_6_out, bit2);
  or or_1 (ALUSrc, bit2, bit1);
  and and_1 (MemWrite, bit1, bit2);
  not not_7 (not_7_out, bit2);
  not not_8 (MemToReg, bit1);
  not not_9 (not_9_out, bit2);
  and and_2 (Jump, bit0, bit2);
  not not_10 (not_10_out, bit0);
  not not_11 (not_11_out, bit1);
  not not_12 (not_12_out, bit1);
  and and_3 (and_3_out, not_1_out, not_2_out, not_3_out);
  and and_4 (and_4_out, bit0, bit1);
  and and_5 (and_5_out, not_4_out, not_5_out);
  and and_6 (and_6_out, bit1, not_6_out);
  and and_7 (MemRead, bit1, not_7_out);
  and and_8 (Branch, bit0, not_9_out);
  and and_9 (ALUOp0, not_10_out, not_11_out);
  and and_10 (and_10_out, not_12_out, bit2);
  or or_2 (RegDst, and_3_out, and_4_out);
  or or_3 (RegWrite, and_5_out, and_6_out);
  or or_4 (ALUOp1, and_10_out, bit0);
endmodule
