// Logisim project MIPS_DAVIT.circ as structural Verilog: 2 circuits, main circuit main
module main (
  output [31:0] out_1,
  output [31:0] out_2
);

  wire button_1_out, clock_1_out;
  wire [31:0] adder_1_out, register_1_q, rom_1_data;

  Register #(.width(32)) register_1 (
    .D(adder_1_out), .Q(register_1_q), .clk(clock_1_out), .clr(button_1_out));  // open: en
  Clock clock_1 (.out(clock_1_out));
  Button button_1 (.out(button_1_out));
  Adder #(.width(32)) adder_1 (.a(32'h4), .b(register_1_q), .out(adder_1_out));  // open: cin, cout
  ROM #(.dataWidth(32)) rom_1 (.addr(register_1_q[9:2]), .data(rom_1_data));  // open: sel
  Banco_de_Registradores banco_de_registradores_1 (
    .Read_register_1(rom_1_data[19:16]), .Read_register_2(rom_1_data[23:20]),
    .Write_register(rom_1_data[27:24]), .CLOCK(clock_1_out), .CLEAR(button_1_out), .Read_data_1(out_1),
    .Read_data_2(out_2));  // open: Write_data, RW

  // Notes on the sheet:
  //   contents of rom_1 (hex, n*v repeats v):
  //   aaaaaaaa ffffffff ffffffff 4*aaaaaaaa
endmodule

module Banco_de_Registradores (
  input  [3:0] Read_register_1,
  input  [3:0] Read_register_2,
  input  [3:0] Write_register,
  input  [31:0] Write_data,
  input  CLOCK,
  input  CLEAR,
  input  RW,
  output [31:0] Read_data_1,
  output [31:0] Read_data_2
);

  wire WE0, WE1, WE2, WE3, WE4, WE5, WE6, WE7, WE9, WE10, WE11, WE12, WE13, WE14, WE15, WE16;
  wire [31:0] Reg0, Reg1, Reg2, Reg3, Reg4, Reg5, Reg6, Reg7, Reg8, Reg9, Reg10, Reg11, Reg12, Reg13, Reg14,
       Reg15;

  Demultiplexer #(.select(4), .enable("false")) demultiplexer_1 (
    .out0(WE0), .out1(WE1), .out2(WE2), .out3(WE3), .out4(WE4), .out5(WE5), .out6(WE6), .out7(WE7),
    .out8(WE9), .out9(WE10), .out10(WE11), .out11(WE12), .out12(WE13), .out13(WE14), .out14(WE15),
    .out15(WE16), .in(RW), .sel(Write_register));
  Multiplexer #(.select(4), .width(32), .enable("false")) multiplexer_1 (
    .in0(Reg0), .in1(Reg1), .in2(Reg2), .in3(Reg3), .in4(Reg4), .in5(Reg5), .in6(Reg6), .in7(Reg7),
    .in8(Reg8), .in9(Reg9), .in10(Reg10), .in11(Reg11), .in12(Reg12), .in13(Reg13), .in14(Reg14),
    .in15(Reg15), .out(Read_data_1), .sel(Read_register_1));
  Register #(.width(32)) register_1 (.D(Write_data), .en(WE0), .Q(Reg0), .clk(CLOCK), .clr(CLEAR));
  Register #(.width(32)) register_2 (.D(Write_data), .en(WE1), .Q(Reg1), .clk(CLOCK), .clr(CLEAR));
  Register #(.width(32)) register_3 (.D(Write_data), .en(WE2), .Q(Reg2), .clk(CLOCK), .clr(CLEAR));
  Register #(.width(32)) register_4 (.D(Write_data), .en(WE3), .Q(Reg3), .clk(CLOCK), .clr(CLEAR));
  Register #(.width(32)) register_5 (.D(Write_data), .en(WE4), .Q(Reg4), .clk(CLOCK), .clr(CLEAR));
  Register #(.width(32)) register_6 (.D(Write_data), .en(WE5), .Q(Reg5), .clk(CLOCK), .clr(CLEAR));
  Register #(.width(32)) register_7 (.D(Write_data), .en(WE6), .Q(Reg6), .clk(CLOCK), .clr(CLEAR));
  Register #(.width(32)) register_8 (.D(Write_data), .en(WE7), .Q(Reg7), .clk(CLOCK), .clr(CLEAR));
  Register #(.width(32)) register_9 (.D(Write_data), .en(WE9), .Q(Reg8), .clk(CLOCK), .clr(CLEAR));
  Register #(.width(32)) register_10 (.D(Write_data), .en(WE10), .Q(Reg9), .clk(CLOCK), .clr(CLEAR));
  Register #(.width(32)) register_11 (.D(Write_data), .en(WE11), .Q(Reg10), .clk(CLOCK), .clr(CLEAR));
  Register #(.width(32)) register_12 (.D(Write_data), .en(WE12), .Q(Reg11), .clk(CLOCK), .clr(CLEAR));
  Register #(.width(32)) register_13 (.D(Write_data), .en(WE13), .Q(Reg12), .clk(CLOCK), .clr(CLEAR));
  Register #(.width(32)) register_14 (.D(Write_data), .en(WE14), .Q(Reg13), .clk(CLOCK), .clr(CLEAR));
  Register #(.width(32)) register_15 (.D(Write_data), .en(WE15), .Q(Reg14), .clk(CLOCK), .clr(CLEAR));
  Register #(.width(32)) register_16 (.D(Write_data), .en(WE16), .Q(Reg15), .clk(CLOCK), .clr(CLEAR));
  Multiplexer #(.select(4), .width(32), .enable("false")) multiplexer_2 (
    .in0(Reg0), .in1(Reg1), .in2(Reg2), .in3(Reg3), .in4(Reg4), .in5(Reg5), .in6(Reg6), .in7(Reg7),
    .in8(Reg8), .in9(Reg9), .in10(Reg10), .in11(Reg11), .in12(Reg12), .in13(Reg13), .in14(Reg14),
    .in15(Reg15), .out(Read_data_2), .sel(Read_register_2));

  // Other names for the same wires on the sheet: CLK = CLOCK; Data[31:0] = Write_data; Read_1[3:0] = Read_register_1;
  //   Read_2[3:0] = Read_register_2; WR[3:0] = Write_register

  // Notes on the sheet:
  //   ENTRADAS
  //   SELEÇÃO DE REGISTRADOR
  //   SAÍDA REGISTRADOR 1
  //   REGISTRADORES
  //   SAÍDA REGISTRADOR 2
endmodule
